# Fritzing sketch STM32与USB转TTL模块 (saved by Fritzing 0.9.10b)

parts:
  元件1 = BluePill
  USBUART1 = CP2102 USB UART Breakout

nets:
  N1: 元件1.A3, USBUART1.TXD
  GND: 元件1.GND, USBUART1.GND
  N2: 元件1.A2, USBUART1.RXD

custom parts:
  CP2102 USB UART Breakout: CP2102 Usb Uart Breakout Board with Battery
